# Fritzing sketch LocalServer (saved by Fritzing 1.0.1rc)
breadboards: 1

parts:
  LED1 = LED - 5mm [color="Red (633nm)" current=0.030 package="5 mm [THT]"]
  LED2 = LED - 5mm [color="Blue (430nm)" current=0.030 package="5 mm [THT]"]
  R1 = Resistor [tolerance=±5% power=0.25 resistance=220 package=THT]
  Part1 = Adafruit T-Cobbler Plus [part_number="Adafruit #1989 and #2028"]
  SG1 = Buzzer 12mm [package=buzzer-12mm-ns]

nets:
  N1: LED1.cathode, LED2.cathode, R1.Pin_0
  N2: LED1.anode, Part1.GPIO17
  N3: LED2.anode, Part1.GPIO18
  N4: R1.Pin_1, Part1.GND, SG1.1
  N5: Part1.GPIO22, SG1.2

custom parts:
  Adafruit T-Cobbler Plus: The Raspberry Pi has landed on the Maker World like a 40-GPIO pinned, quad-USB ported, credit card sized bomb of DIY joy. And while you can use most of our great Model B accessories by hooking up our downgrade cable, its probably a good time to upgrade your set up and accessorize using all of the 40 pins. That's why we now carry the Assembled Adafruit Pi T-Cobbler Plus - Breakout + Cable for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
