# Fritzing sketch currentMotor (saved by Fritzing 1.0.1rc)
breadboards: 1

parts:
  IC1 = L293D [package=THT]
  Part1 = Adafruit T-Cobbler Plus [part_number="Adafruit #1989 and #2028"]
  U1 = ESP32-38PinWide [part_number=ESP32-38PinWide]  # not connected
  Part2 = Arduino Uno (Rev3) - ICSP  # not connected
  M1 = DC Motor [voltage_(max)=6V voltage_(min)=3V]

nets:
  N1: IC1.Enable_1, Part1.GPIO22
  N2: IC1.In_1, Part1.GPIO27
  N3: IC1.Out_1_(_Controlled_by_Enable_1_), M1.pin_2
  N4: IC1.0V, Part1.GND
  N5: IC1.Out_2_(_Controlled_by_Enable_1_), M1.pin_1
  N6: IC1.In_2, Part1.GPIO17
  N7: IC1.+V, Part1.+5V

custom parts:
  Adafruit T-Cobbler Plus: The Raspberry Pi has landed on the Maker World like a 40-GPIO pinned, quad-USB ported, credit card sized bomb of DIY joy. And while you can use most of our great Model B accessories by hooking up our downgrade cable, its probably a good time to upgrade your set up and accessorize using all of the 40 pins. That's why we now carry the Assembled Adafruit Pi T-Cobbler Plus - Breakout + Cable for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
  ESP32-38PinWide: Generic 38-Pin ESP32 with wide format (only access to one side of pins on a breadboard) based on Stephen Lilley's HiLetgo ESP-WROOM-32 ESP32 ESP-32S Development Board.
